# Fritzing sketch BlinkAll (saved by Fritzing 0.9.2b)

parts:
  Součástka1 = Arduino Uno (Rev3)
  R1 = Resistor [tolerance=±5% resistance=220 package=THT]
  LED1 = LED - 5mm [color="Blue (525nm)" package="5 mm [THT]"]
  LED2 = LED - 5mm [color="Red (633nm)" package="5 mm [THT]"]
  LED3 = LED - 5mm [color="Green (565nm)" package="5 mm [THT]"]
  LED4 = LED - 5mm [color="Red (633nm)" package="5 mm [THT]"]
  R2 = Resistor [tolerance=±5% resistance=220 package=THT]
  R3 = Resistor [tolerance=±5% resistance=220 package=THT]
  R4 = Resistor [tolerance=±5% resistance=220 package=THT]

nets:
  N1: Součástka1.GND, R1.Pin_0, R2.Pin_0, R3.Pin_0, R4.Pin_0
  N2: Součástka1.D2, LED1.anode
  N3: Součástka1.D3_PWM, LED3.anode
  N4: Součástka1.D4, LED2.anode
  N5: Součástka1.D5_PWM, LED4.anode
  N6: LED2.cathode, R3.Pin_1
  N7: LED3.cathode, R4.Pin_1
  N8: LED4.cathode, R2.Pin_1
