# Fritzing sketch Fade (saved by Fritzing 0.9.2b)

parts:
  S1 = Pushbutton [package="[THT]"]
  S2 = Pushbutton [package="[THT]"]
  R1 = Resistor [tolerance=±5% resistance=220 package=THT]
  LED1 = LED - 5mm [color="Red (633nm)" package="5 mm [THT]"]
  Součástka1 = Arduino Uno (Rev3)

nets:
  N1: S1.Pin_2, Součástka1.D10_PWM/SS
  N2: S1.Pin_3, S1.Pin_4, S2.Pin_3, S2.Pin_4, R1.Pin_0, Součástka1.GND
  N3: S2.Pin_1, S2.Pin_2, Součástka1.D9_PWM
  N4: R1.Pin_1, LED1.cathode
  N5: LED1.anode, Součástka1.D5_PWM
