# Fritzing sketch RGB (saved by Fritzing 0.9.3b)

parts:
  Součástka1 = Arduino Uno (Rev3)
  LED1 = Super Flux RGB LED (com. anode)

nets:
  N1: Součástka1.D9_PWM, LED1.red_cathode
  N2: Součástka1.D5_PWM, LED1.green_cathode
  N3: Součástka1.D6_PWM, LED1.blue_cathode
  N4: Součástka1.5V, LED1.common_anode
