# Fritzing sketch Semafor (saved by Fritzing 0.9.3b)

parts:
  Součástka1 = Arduino Uno (Rev3)
  LED1 = LED - 3mm [color="Red (633nm)" package="3 mm [THT]"]
  LED2 = LED - 3mm [color="Yellow (592nm)" package="3 mm [THT]"]
  LED3 = LED - 3mm [color="Green (560nm)" package="3 mm [THT]"]
  S1 = Pushbutton [package="[THT]"]
  R1 = Resistor [tolerance=±5% resistance=220 package="2010 [SMD]"]
  R2 = Resistor [tolerance=±5% resistance=220 package="2010 [SMD]"]
  R3 = Resistor [tolerance=±5% resistance=220 package="2010 [SMD]"]
  R4 = Resistor [tolerance=±5% resistance=220 package="2010 [SMD]"]

nets:
  N1: Součástka1.A2, R3.Pin_0
  N2: Součástka1.A3, R4.Pin_0
  N3: Součástka1.D13/SCK, R2.Pin_0
  N4: Součástka1.D2, S1.Pin_1, S1.Pin_2, R1.Pin_0
  N5: Součástka1.5V, R1.Pin_1
  N6: Součástka1.GND, LED1.cathode, LED2.cathode, LED3.cathode, S1.Pin_4
  N7: LED1.anode, R3.Pin_1
  N8: LED2.anode, R4.Pin_1
  N9: LED3.anode, R2.Pin_1
