# Fritzing sketch Temperature (saved by Fritzing 0.9.2b)

parts:
  Součástka1 = Arduino Uno (Rev3)
  R6 = Resistor [tolerance=±5% resistance=220 package=THT]
  R7 = Temperature Sensor (Thermistor) [thermistor_type=NTC package=THT]
  U1 = 7-SEGMENT-4DIGIT [package=7-segment-4digit-youngsun]  # not connected

nets:
  N1: Součástka1.A0, R6.Pin_0, R7.pin_0
  N2: Součástka1.5V, R7.pin_1
  N3: Součástka1.GND, R6.Pin_1
